# Fritzing sketch labyrinth_sketch (saved by Fritzing 0.9.2b)
breadboards: 1

parts:
  BeagleBone1 = BeagleBone Black
  J1 = Basic Servo
  J2 = Basic Servo
  JACK1 = 2.1mm Barrel Jack with Terminal Block

nets:
  GND: BeagleBone1.no_name_yet#1, J1.gnd, J2.gnd, JACK1.NEG
  VCC: BeagleBone1.no_name_yet#5, J1.vcc, J2.vcc, JACK1.POS
  N1: BeagleBone1.no_name_yet#14, J1.pulse
  N2: BeagleBone1.no_name_yet#16, J2.pulse

custom parts:
  BeagleBone Black: BeagleBone Black rev. A5B
